# Fritzing sketch car (saved by Fritzing 0.9.3b)
breadboards: 1

parts:
  Part1 = Arduino Uno (Rev3) - ICSP
  IC1 = L293D [package=THT]
  VCC1 = 4 x AAA Battery Mount
  M1 = DC Motor
  M2 = DC Motor
  Part2 = Bluetooth HC-05 Macho
  R1 = Resistor [tolerance=±5% resistance=220 package="0402 [SMD]"]
  R2 = Resistor [tolerance=±5% resistance=220 package="0402 [SMD]"]

nets:
  N1: Part1.D9_PWM, IC1.Enable_1
  N2: Part1.D10_PWM/SS, IC1.Enable_2
  GND: Part1.GND, IC1.0V, VCC1.-, Part2.GND, R1.Pin_0
  N3: Part1.D2, Part2.TXD
  N4: Part1.D3_PWM, R2.Pin_0
  N5: Part1.D4, IC1.In_1
  N6: Part1.D5_PWM, IC1.In_2
  N7: Part1.D6_PWM, IC1.In_4
  N8: Part1.D7, IC1.In_3
  5V: Part1.5V, IC1.+V, Part2.VCC
  N9: IC1.Out_1_(_Controlled_by_Enable_1_), M2.pin_2
  N10: IC1.Out_2_(_Controlled_by_Enable_1_), M2.pin_1
  N11: IC1.+Vmotor, VCC1.+
  N12: IC1.Out_3_(_Controlled_by_Enable_2_), IC1.Out_4_(_Controlled_by_Enable_2_), M1.pin_2
  N13: Part2.RXD, R1.Pin_1, R2.Pin_1
