# Fritzing sketch hc-05 setup (saved by Fritzing 0.9.3b)
breadboards: 1

parts:
  Part1 = Arduino Uno (Rev3) - ICSP
  R1 = Resistor [tolerance=±5% resistance=1k package="2010 [SMD]"]
  R2 = Resistor [tolerance=±5% resistance=2.2k package="2010 [SMD]"]
  Part2 = Bluetooth HC-05 Macho  # not connected

nets:
  N1: Part1.D3_PWM, R1.Pin_0
  N2: Part1.GND, R2.Pin_1
  N3: R1.Pin_1, R2.Pin_0

notes:
  2K
  1K
